# Fritzing sketch SDS (saved by Fritzing 0.9.3b)
breadboards: 1

parts:
  Arduino = Arduino Uno (Rev3)
  S1 = Momentary Switch [package=ksa_sealed_tac_switch]
  LED1 = LED - 5mm [color="Red (633nm)" package="5 mm [THT]"]
  HC-SR501 = HC-SR501 Body Sensor Module
  R1 = Resistor [tolerance=±5% resistance=1k package=THT]

nets:
  N1: Arduino.D2, S1.2
  N2: Arduino.D4, LED1.anode
  N3: Arduino.D7, HC-SR501.OUT
  5V: Arduino.5V, S1.3, HC-SR501.VCC
  GND: Arduino.GND, LED1.cathode, HC-SR501.GND, R1.Pin_1
  N4: S1.1, R1.Pin_0

custom parts:
  HC-SR501 Body Sensor Module: Pyroelectric Infrared PIR Motion Sensor Detector Module
